# Fritzing sketch panelized (saved by Fritzing 0.9.3b)
circuit board: 8.50478cm x 5.30001cm
breadboards: 1

parts:
  X1 = USB Connectors [package=usb-a-pcb]
  J9 = longpad pin header, 4 pins [form="long pad"]
  J10 = longpad pin header, 4 pins [form="long pad"]
  C1 = Ceramic Capacitor [capacitance=0.1µF package="0805 [SMD, multilayer]"]
  R1 = Resistor [tolerance=±5% resistance=68 package="0805 [SMD]"]
  R2 = Resistor [tolerance=±5% resistance=68 package="0805 [SMD]"]
  R3 = Resistor [tolerance=±5% resistance=1.5k package="0805 [SMD]"]
  Z1 = DIODE-ZENER [part_number="3V6 Zener BZY55C3V6 RYG" package=sod-323]
  Z2 = DIODE-ZENER [part_number="3V6 Zener BZY55C3V6 RYG" package=sod-323]
  Pad1 = Pad [width=7.902222222222222 height=9.0311111111111106 connect=center]
  R4 = Resistor [tolerance=±5% resistance=10k package="0805 [SMD]"]
  J1 = Solder Jumper [package=sj_2s-trace]
  ATtiny85 = ATTINY13 [package=so]
  USB = mystery part, 6 pins [chip_label=?]
  J15 = female pin header, 4 pins [form="♀ (female)"]  # not connected
  J16 = female pin header, 4 pins [form="♀ (female)"]  # not connected
  J17 = female pin header, 4 pins [form="♀ (female)"]  # not connected
  J19 = female pin header, 4 pins [form="♀ (female)"]  # not connected
  J20 = female pin header, 4 pins [form="♀ (female)"]  # not connected
  J21 = female pin header, 4 pins [form="♀ (female)"]  # not connected
  J23 = female pin header, 3 pins [form="♀ (female)"]  # not connected
  J24 = female pin header, 3 pins [form="♀ (female)"]  # not connected
  J27 = female pin header, 6 pins [form="♀ (female)"]  # not connected
  J28 = double row female pin header, 18 pins [form="♀ (female)"]  # not connected
  J25 = female pin header, 3 pins [form="♀ (female)"]  # not connected
  J7 = double row female pin header, 18 pins [form="♀ (female)"]  # not connected
  J26 = female pin header, 3 pins [form="♀ (female)"]  # not connected
  J13 = female pin header, 6 pins [form="♀ (female)"]  # not connected
  J29 = double row female pin header, 18 pins [form="♀ (female)"]  # not connected
  J30 = double row female pin header, 18 pins [form="♀ (female)"]  # not connected
  Pad2 = Pad [width=1 height=12.587111111111112 connect=center]  # not connected
  Pad3 = Pad [width=1 height=12.587111111111112 connect=center]  # not connected
  Pad4 = Pad [width=1 height=2.54 connect=center]  # not connected
  Pad5 = Pad [width=1 height=2.54 connect=center]  # not connected
  Pad6 = Pad [width=1 height=2.54 connect=center]  # not connected
  Pad7 = Pad [width=1 height=2.54 connect=center]  # not connected
  Pad8 = Pad [width=1 height=2.54 connect=center]  # not connected
  Pad9 = Pad [width=1 height=2.54 connect=center]  # not connected
  Pad10 = Pad [width=1 height=2.54 connect=center]  # not connected
  Pad11 = Pad [width=1 height=2.54 connect=center]  # not connected
  Pad12 = Pad [width=1 height=2.54 connect=center]  # not connected
  Pad13 = Pad [width=1 height=2.54 connect=center]  # not connected
  Pad14 = Pad [width=1 height=2.54 connect=center]  # not connected
  Pad15 = Pad [width=1 height=2.54 connect=center]  # not connected
  Pad16 = Pad [width=1 height=2.54 connect=center]  # not connected
  Pad17 = Pad [width=1 height=2.54 connect=center]  # not connected
  Pad18 = Pad [width=1 height=2.54 connect=center]  # not connected
  Pad19 = Pad [width=1 height=2.54 connect=center]  # not connected
  Pad20 = Pad [width=1 height=2.54 connect=center]  # not connected
  Pad21 = Pad [width=1 height=2.54 connect=center]  # not connected
  Pad22 = Pad [width=1 height=5 connect=center]  # not connected
  Pad23 = Pad [width=1 height=5 connect=center]  # not connected
  Pad24 = Pad [width=1 height=5 connect=center]  # not connected
  Pad25 = Pad [width=1 height=5 connect=center]  # not connected
  Pad26 = Pad [width=1 height=8 connect=center]  # not connected
  Pad27 = Pad [width=1 height=8 connect=center]  # not connected
  Pad28 = Pad [width=1 height=8 connect=center]  # not connected
  Pad29 = Pad [width=1 height=8 connect=center]  # not connected
  Pad30 = Pad [width=1 height=8 connect=center]  # not connected
  Pad31 = Pad [width=1 height=8 connect=center]  # not connected
  RESET = Pushbutton [package=THT]
  PWR_LED = LED - 5mm [color="Red (633nm)" package="5 mm [THT]"]
  R5_1K = Resistor [tolerance=±5% resistance=220 package=THT]
  J12 = longpad pin header, 1 pin [form="long pad"]
  J11 = longpad pin header, 1 pin [form="long pad"]
  R5 = Resistor [tolerance=±5% resistance=10k package="0805 [SMD]"]
  J2 = Solder Jumper [package=sj_2s-trace]
  J3 = Solder Jumper [package=sj_2s-no]
  J34 = female pin header, 4 pins [form="♀ (female)"]
  J35 = female pin header, 4 pins [form="♀ (female)"]
  ATtiny_85 = ATTINY13 [package=so]
  AVR_ISP = AVR ISP 6 Pin [package=2x3]
  USB3 = mystery part, 6 pins [chip_label=?]

nets:
  N1: X1.VBUS, J10.pin4, C1.1, R3.Pin_1, ATtiny85.VCC, USB.pin1, PWR_LED.anode, J12.pin1, J2.2
  GND: X1.GND, J9.pin1, C1.0, Z1.A, Z2.A, ATtiny85.GND, USB.pin4, RESET.leg1, R5_1K.Pin_1, J11.pin1, J3.1
  N2: X1.D-, R1.Pin_1, R3.Pin_0, Z1.C
  N3: X1.D+, R2.Pin_1, Z2.C
  N4: J9.pin2, R2.Pin_0, ATtiny85.PB4(ADC2)
  N5: J9.pin3, R1.Pin_0, ATtiny85.PB3(ADC3)
  N6: J9.pin4, ATtiny85.PB5(NRES), USB.pin5, RESET.leg0, R5.Pin_0
  N7: J10.pin1, ATtiny85.PB0(MOSI), USB.pin2, J3.2
  N8: J10.pin2, ATtiny85.PB1(MISO), USB.pin6
  N9: J10.pin3, J1.2, ATtiny85.PB2(SCK_ADC1), USB.pin3
  N10: Pad1.pad, R4.Pin_1
  N11: R4.Pin_0, J1.1
  N12: PWR_LED.cathode, R5_1K.Pin_0
  N13: R5.Pin_1, J2.1
  N14: J34.pin1, ATtiny_85.PB5(NRES)
  N15: J34.pin2, ATtiny_85.PB3(ADC3)
  N16: J34.pin3, ATtiny_85.PB4(ADC2)
  N17: J34.pin4, ATtiny_85.GND
  N18: J35.pin1, ATtiny_85.VCC
  N19: J35.pin2, ATtiny_85.PB2(SCK_ADC1)
  N20: J35.pin3, ATtiny_85.PB1(MISO)
  N21: J35.pin4, ATtiny_85.PB0(MOSI)
  N22: AVR_ISP.1, USB3.pin6
  N23: AVR_ISP.2, USB3.pin1
  N24: AVR_ISP.3, USB3.pin3
  N25: AVR_ISP.4, USB3.pin2
  N26: AVR_ISP.5, USB3.pin5
  N27: AVR_ISP.6, USB3.pin4

notes:
  Exploit.Agency
  www.LegacySecurityGroup.com
  Corey Harding
  Information Security Research and Development
  8    VCC
  7    PB2
  6    PB1
  5    PB0
  PB4    3
  PB3    2
  GND    4
  PB5    1
  8
  +5V
  GND
  MISO
  RST
  SCK
  VTG
  MOSI
  Touch
  - Open a text editor
  - Touch copper pad
  Rev 1f
  AVR ISP
  Prototyping Area
  Contact@LegacySecurityGroup.com
  - Attach via USB
  3
  2
  4
  1
  6
  5
  7
  POGO PIN ADAPTER
